// Logisim project 3BITFULLADDERNAND.circ as structural Verilog: 1 circuit, main circuit main
module main (
  input  in_1,
  input  in_2,
  input  in_3,
  output out_4,
  output out_5
);

  wire nand_2_out, nand_3_out, nand_4_out, nand_5_out, nand_6_out, nand_7_out;

  // NAND_Gate nand_1 has open pins: in0=in_1, in1=in_2, out=open
  nand nand_2 (nand_2_out, in_1, in_3);
  nand nand_3 (nand_3_out, in_3, in_2);
  nand nand_4 (nand_4_out, nand_2_out, nand_3_out);
  nand nand_5 (nand_5_out, nand_4_out, in_3);
  nand nand_6 (nand_6_out, nand_4_out, nand_5_out);
  nand nand_7 (nand_7_out, nand_5_out, in_3);
  nand nand_8 (out_4, nand_6_out, nand_7_out);
  nand nand_9 (out_5, nand_5_out, in_3);
endmodule
