// Logisim project 4 bit carry look.circ as structural Verilog: 1 circuit, main circuit main
module main (
  input  in_1,
  input  in_2,
  input  in_3,
  input  in_4,
  input  in_5,
  input  in_6,
  input  in_7,
  input  in_8,
  output out_9,
  output out_10,
  output out_11,
  output out_12
);

  wire and_1_out, and_2_out, and_3_out, and_4_out, and_5_out, and_6_out, and_7_out, and_8_out, and_9_out,
       and_10_out, and_11_out, and_12_out, and_13_out, and_14_out, xor_1_out, xor_2_out, xor_3_out, xor_4_out;

  xor xor_1 (xor_1_out, in_1, in_2);
  and and_1 (and_1_out, in_1, in_2);
  xor xor_2 (xor_2_out, in_3, in_4);
  and and_2 (and_2_out, in_3, in_4);
  xor xor_3 (xor_3_out, in_5, in_6);
  and and_3 (and_3_out, in_5, in_6);
  xor xor_4 (xor_4_out, in_7, in_8);
  and and_4 (and_4_out, in_7, in_8);
  and and_5 (and_5_out, xor_2_out, xor_1_out);
  buf and_6 (and_6_out, and_3_out);  // AND_Gate
  buf and_7 (and_7_out, xor_2_out);  // AND_Gate
  and and_8 (and_8_out, xor_1_out, and_2_out);
  and and_9 (and_9_out, xor_2_out, and_3_out);
  and and_10 (and_10_out, xor_2_out, and_4_out);
  and and_11 (and_11_out, and_4_out, xor_3_out);
  and and_12 (and_12_out, xor_3_out, and_4_out);
  and and_13 (and_13_out, xor_3_out, and_4_out);
  and and_14 (and_14_out, xor_4_out, and_4_out);
  or or_1 (out_10, and_9_out, and_2_out);
  buf or_2 (out_11, and_3_out);  // OR_Gate
  or or_3 (out_12, and_14_out, and_4_out);
  or or_4 (out_9, and_6_out, and_1_out);
endmodule
